// Logisim project COA.circ as structural Verilog: 5 circuits, main circuit PROJECT1
module main (
  input  CLOCK,
  input  [1:0] A_SELECT,
  input  [7:0] INPUT_C,
  input  [1:0] B_SELECT,
  input  [1:0] C_SELECT,
  input  C_CONTROL,
  output [7:0] R0,
  output [7:0] R1,
  output [7:0] R2,
  output [7:0] R3,
  output [7:0] OUTPUT_A,
  output [7:0] OUTPUT_B
);

  wire [7:0] demultiplexer_1_out0, demultiplexer_1_out1, demultiplexer_1_out2, demultiplexer_1_out3;

  Demultiplexer #(.select(2), .width(8), .tristate("true")) demultiplexer_1 (
    .out0(demultiplexer_1_out0), .out1(demultiplexer_1_out1), .out2(demultiplexer_1_out2),
    .out3(demultiplexer_1_out3), .in(INPUT_C), .sel(C_SELECT), .en(C_CONTROL));
  Register register_1 (.D(demultiplexer_1_out0), .Q(R0), .clk(CLOCK));  // open: en, clr
  Register register_2 (.D(demultiplexer_1_out1), .Q(R1), .clk(CLOCK));  // open: en, clr
  Register register_3 (.D(demultiplexer_1_out2), .Q(R2), .clk(CLOCK));  // open: en, clr
  Register register_4 (.D(demultiplexer_1_out3), .Q(R3), .clk(CLOCK));  // open: en, clr
  Multiplexer #(.select(2), .width(8)) multiplexer_1 (
    .in0(R0), .in1(R1), .in2(R2), .in3(R3), .out(OUTPUT_A), .sel(A_SELECT));  // open: en
  Multiplexer #(.select(2), .width(8), .disabled(0)) multiplexer_2 (
    .in0(R0), .in1(R1), .in2(R2), .in3(R3), .out(OUTPUT_B), .sel(B_SELECT));  // open: en
endmodule

module ALU (
  input  carry_in,
  input  [7:0] Register_1,
  input  [7:0] Register_2,
  input  [3:0] OPERAND,
  output SIGN,
  output [7:0] \output 
);

  wire comparator_1_eq, comparator_2_eq, comparator_3_eq, comparator_4_eq, comparator_5_eq, comparator_6_eq,
       comparator_6_gt, subtractor_1_bout;
  wire [7:0] adder_1_out, and_1_out, multiplier_1_out, or_1_out, subtractor_1_out, xor_1_out;

  Comparator #(.width(4), .mode("unsigned")) comparator_1 (
    .a(OPERAND), .b(4'b0000), .eq(comparator_1_eq));  // open: gt, lt
  Comparator #(.width(4), .mode("unsigned")) comparator_2 (
    .a(OPERAND), .b(4'b0001), .eq(comparator_2_eq));  // open: gt, lt
  Comparator #(.width(4), .mode("unsigned")) comparator_3 (
    .a(OPERAND), .b(4'b0010), .eq(comparator_3_eq));  // open: gt, lt
  Comparator #(.width(4), .mode("unsigned")) comparator_4 (
    .a(OPERAND), .b(4'b0011), .eq(comparator_4_eq));  // open: gt, lt
  Comparator #(.width(4), .mode("unsigned")) comparator_5 (
    .a(OPERAND), .b(4'b0100), .eq(comparator_5_eq));  // open: gt, lt
  Comparator #(.width(4), .mode("unsigned")) comparator_6 (
    .a(OPERAND), .b(4'b0101), .gt(comparator_6_gt), .eq(comparator_6_eq));  // open: lt
  Adder adder_1 (.a(Register_1), .b(Register_2), .out(adder_1_out), .cin(carry_in));  // open: cout
  assign \output  = comparator_1_eq ? adder_1_out : 8'bz;  // Controlled_Buffer controlled_buffer_1
  Subtractor subtractor_1 (
    .a(Register_1), .b(Register_2), .out(subtractor_1_out), .bout(subtractor_1_bout));  // open: bin
  assign \output  = comparator_2_eq ? subtractor_1_out : 8'bz;  // Controlled_Buffer controlled_buffer_2
  Multiplier multiplier_1 (.a(Register_1), .b(Register_2), .out(multiplier_1_out));  // open: cin, cout
  assign and_1_out = Register_1 & Register_2;  // AND_Gate and_1, 8 bits wide
  assign or_1_out = Register_1 | Register_2;  // OR_Gate or_1, 8 bits wide
  assign xor_1_out = Register_1 ^ Register_2;  // XOR_Gate xor_1, 8 bits wide
  assign SIGN = comparator_2_eq ? subtractor_1_bout : 1'bz;  // Controlled_Buffer controlled_buffer_3
  assign \output  = comparator_3_eq ? multiplier_1_out : 8'bz;  // Controlled_Buffer controlled_buffer_4
  assign \output  = comparator_4_eq ? and_1_out : 8'bz;  // Controlled_Buffer controlled_buffer_5
  assign \output  = comparator_5_eq ? or_1_out : 8'bz;  // Controlled_Buffer controlled_buffer_6
  assign \output  = comparator_6_eq ? xor_1_out : 8'bz;  // Controlled_Buffer controlled_buffer_7
  assign \output  = comparator_6_gt ? Register_2 : 8'bz;  // Controlled_Buffer controlled_buffer_8
endmodule

module PROGRAM_COUNTER (
  input  [7:0] ADDRESS,
  input  IN_SELECT,
  input  Set_PC,
  input  CLOCK,
  input  PC_Enable,
  output [7:0] OUTPUT,
  output [7:0] PC_TEMP
);

  wire multiplexer_1_out;
  wire [7:0] adder_1_out, multiplexer_2_out, subtractor_1_out;

  Multiplexer #(.enable("false")) multiplexer_1 (.in0(1'b0), .in1(1'b1), .out(multiplexer_1_out), .sel(PC_Enable));
  Register PC (.D(adder_1_out), .en(multiplexer_1_out), .Q(OUTPUT), .clk(CLOCK), .clr(Set_PC));
  Register u_PC_TEMP (.D(OUTPUT), .Q(PC_TEMP), .clk(CLOCK));  // open: en, clr
  Multiplexer #(.width(8), .enable("false")) multiplexer_2 (
    .in0(8'h1), .in1(subtractor_1_out), .out(multiplexer_2_out), .sel(IN_SELECT));
  Adder adder_1 (.a(multiplexer_2_out), .b(OUTPUT), .out(adder_1_out));  // open: cin, cout
  Subtractor subtractor_1 (.a(ADDRESS), .b(OUTPUT), .out(subtractor_1_out));  // open: bin, bout
endmodule

module PROJECT1 (
  input  set_PC,
  output [7:0] out_2,
  output [7:0] out_3,
  output [7:0] out_4,
  output [7:0] out_5,
  output [2:0] out_6
);

  wire a, and_1_out, c_select, clock, comparator_1_eq, comparator_2_lt, mux_select, mux_y, not_1_out,
       not_3_out, pc_enable, reg_select, reg_y, rz_enable, store1, store2, store3, store4;
  wire [1:0] B_SELECT, C_A_SELECT;
  wire [3:0] bbb;
  wire [7:0] address, alu_1_output, controlled_buffer_1_out, input_c, main_1_output_a, main_1_output_b,
       multiplexer_1_out, multiplexer_2_out, multiplexer_3_out, multiplexer_4_out, program_counter_1_output,
       RA_q, RB_q, RM_q, RZ_q;

  Control_Circuit control_circuit_1 (
    .\input (bbb), .clock(clock), .counter(out_6), .PC_Enable(pc_enable), .Store_1(store1), .store3(store3),
    .Store_2(store2), .muxy(mux_y), .rz_enable(rz_enable), .reg_y(reg_y), .REG_SELECT(reg_select),
    .MUX_SELECT(mux_select), .C_SELECT(c_select), .store4(store4));
  Register RA (.D(main_1_output_a), .en(reg_select), .Q(RA_q), .clk(clock));  // open: clr
  Register RZ (.D(alu_1_output), .en(rz_enable), .Q(RZ_q), .clk(clock));  // open: clr
  Multiplexer #(.width(8), .enable("false")) multiplexer_1 (
    .in0(RZ_q), .in1(controlled_buffer_1_out), .out(multiplexer_1_out), .sel(mux_y));
  main main_1 (
    .CLOCK(clock), .INPUT_C(input_c), .C_SELECT(C_A_SELECT), .A_SELECT(C_A_SELECT), .B_SELECT(B_SELECT),
    .R0(out_5), .R1(out_4), .R2(out_3), .R3(out_2), .OUTPUT_A(main_1_output_a), .OUTPUT_B(main_1_output_b),
    .C_CONTROL(c_select));
  Register RB (.D(main_1_output_b), .en(reg_select), .Q(RB_q), .clk(clock));  // open: clr
  Multiplexer #(.width(8), .enable("false")) multiplexer_2 (
    .in0(RB_q), .in1(address), .out(multiplexer_2_out), .sel(mux_select));
  ALU alu_1 (
    .Register_1(RA_q), .Register_2(multiplexer_2_out), .OPERAND(bbb), .\output (alu_1_output));  // open: carry_in, SIGN
  Register register_1 (.D(multiplexer_1_out), .en(reg_y), .Q(input_c), .clk(clock));  // open: clr
  Register RM (.D(RA_q), .en(rz_enable), .Q(RM_q), .clk(clock));  // open: clr
  and and_1 (and_1_out, comparator_1_eq, a);
  Comparator #(.width(4), .mode("unsigned")) comparator_1 (.a(bbb), .b(4'b1001), .eq(comparator_1_eq));  // open: gt, lt
  not not_1 (not_1_out, and_1_out);
  Multiplexer #(.width(8), .enable("false")) multiplexer_3 (
    .in0(address), .in1(program_counter_1_output), .out(multiplexer_3_out), .sel(not_1_out));
  Multiplexer #(.width(8), .enable("false")) multiplexer_4 (
    .in0(program_counter_1_output), .in1(RZ_q), .out(multiplexer_4_out), .sel(store3));
  Clock clock_1 (.out(clock));
  PROGRAM_COUNTER program_counter_1 (
    .ADDRESS(multiplexer_3_out), .IN_SELECT(and_1_out), .Set_PC(set_PC), .CLOCK(clock),
    .PC_Enable(pc_enable), .OUTPUT(program_counter_1_output));  // open: PC_TEMP
  assign controlled_buffer_1_out = store1 ? RM_q : 8'bz;  // Controlled_Buffer controlled_buffer_1
  Comparator #(.width(3), .mode("unsigned")) comparator_2 (
    .a(out_6), .b(3'b100), .lt(comparator_2_lt));  // open: gt, eq
  not not_2 (a, comparator_2_lt);
  not not_3 (not_3_out, store1);
  Register register_2 (.D(controlled_buffer_1_out), .en(store4), .Q(address), .clk(clock));  // open: clr
  RAM ram_1 (.addr(multiplexer_4_out), .data(controlled_buffer_1_out), .clk(clock), .ld(not_3_out));  // open: sel, clr
  Register INSTRUCTION_REGISTER (
    .D(controlled_buffer_1_out), .en(store2), .Q({bbb, C_A_SELECT, B_SELECT}), .clk(clock));  // open: clr

  // Other names for the same wires on the sheet: counter_value[2:0] = out_6; R0[7:0] = out_5; R1[7:0] = out_4;
  //   R2[7:0] = out_3; R3[7:0] = out_2
endmodule

// control_circuit
module Control_Circuit (
  input  clock,
  input  [3:0] \input ,
  output [2:0] counter,
  output PC_Enable,
  output Store_1,
  output store3,
  output Store_2,
  output muxy,
  output rz_enable,
  output reg_y,
  output REG_SELECT,
  output MUX_SELECT,
  output C_SELECT,
  output store4
);

  wire and_1_out, and_4_out, comparator_1_eq, comparator_2_eq, comparator_3_eq, comparator_4_eq,
       comparator_5_eq, comparator_6_eq, comparator_6_lt, comparator_8_eq, comparator_9_eq, comparator_10_eq,
       comparator_12_eq, comparator_13_eq, comparator_13_lt, comparator_14_eq, comparator_14_lt,
       comparator_15_eq, comparator_17_eq, comparator_19_eq, or_1_out, or_2_out, or_3_out, or_4_out, or_5_out;

  Counter #(.width(3), .max('h6)) counter_1 (.Q(counter), .clk(clock));  // open: load, D, count, carry, clr
  Comparator #(.width(3), .mode("unsigned")) comparator_1 (
    .a(3'b000), .b(counter), .eq(comparator_1_eq));  // open: gt, lt
  Comparator #(.width(3), .mode("unsigned")) comparator_2 (
    .a(counter), .b(3'b010), .eq(comparator_2_eq));  // open: gt, lt
  Comparator #(.width(3), .mode("unsigned")) comparator_3 (
    .a(3'b101), .b(counter), .eq(comparator_3_eq));  // open: gt, lt
  Comparator #(.width(4), .mode("unsigned")) comparator_4 (
    .a(\input ), .b(4'b1001), .eq(comparator_4_eq));  // open: gt, lt
  Comparator #(.width(3), .mode("unsigned")) comparator_5 (
    .a(counter), .b(3'b101), .eq(comparator_5_eq));  // open: gt, lt
  Comparator #(.width(4), .mode("unsigned")) comparator_6 (
    .a(\input ), .b(4'b1000), .eq(comparator_6_eq), .lt(comparator_6_lt));  // open: gt
  Comparator #(.width(3), .mode("unsigned")) comparator_7 (.a(counter), .b(3'b001), .eq(Store_2));  // open: gt, lt
  Comparator #(.width(3), .mode("unsigned")) comparator_8 (
    .a(counter), .b(3'b101), .eq(comparator_8_eq));  // open: gt, lt
  Comparator #(.width(4), .mode("unsigned")) comparator_9 (
    .a(\input ), .b(4'b0111), .eq(comparator_9_eq));  // open: gt, lt
  and and_1 (and_1_out, comparator_3_eq, comparator_4_eq);
  and and_2 (Store_1, comparator_5_eq, comparator_6_eq);
  and and_3 (reg_y, comparator_6_lt, comparator_8_eq);
  Comparator #(.width(4), .mode("unsigned")) comparator_10 (
    .a(\input ), .b(4'b1000), .eq(comparator_10_eq));  // open: gt, lt
  or or_1 (or_1_out, comparator_10_eq, comparator_9_eq, comparator_4_eq);
  and and_4 (and_4_out, comparator_2_eq, or_1_out);
  Comparator #(.width(3), .mode("unsigned")) comparator_11 (.a(counter), .b(3'b011), .eq(REG_SELECT));  // open: gt, lt
  Comparator #(.width(3), .mode("unsigned")) comparator_12 (
    .a(counter), .b(3'b100), .eq(comparator_12_eq));  // open: gt, lt
  Comparator #(.width(4), .mode("unsigned")) comparator_13 (
    .a(\input ), .b(4'b0111), .eq(comparator_13_eq), .lt(comparator_13_lt));  // open: gt
  Comparator #(.width(4), .mode("unsigned")) comparator_14 (
    .a(\input ), .b(4'b1000), .eq(comparator_14_eq), .lt(comparator_14_lt));  // open: gt
  Comparator #(.width(3), .mode("unsigned")) comparator_15 (
    .a(counter), .b(3'b110), .eq(comparator_15_eq));  // open: gt, lt
  Comparator #(.width(3), .mode("unsigned")) comparator_16 (.a(counter), .b(3'b011), .eq(store4));  // open: gt, lt
  or or_2 (or_2_out, comparator_1_eq, and_4_out, and_1_out);
  Comparator #(.width(4), .mode("unsigned")) comparator_17 (
    .a(\input ), .b(4'b1010), .eq(comparator_17_eq));  // open: gt, lt
  Comparator #(.width(3), .mode("unsigned")) comparator_18 (.a(counter), .b(3'b100), .eq(rz_enable));  // open: gt, lt
  or or_3 (or_3_out, REG_SELECT, comparator_12_eq);
  or or_4 (or_4_out, comparator_13_eq, comparator_14_eq);
  Multiplexer #(.enable("false")) multiplexer_1 (.in0(or_2_out), .in1(1'b0), .out(PC_Enable), .sel(comparator_17_eq));
  and and_5 (MUX_SELECT, or_3_out, or_4_out);
  and and_6 (C_SELECT, comparator_14_lt, comparator_15_eq);
  Comparator #(.width(4), .mode("unsigned")) comparator_19 (
    .a(\input ), .b(4'b0111), .eq(comparator_19_eq));  // open: gt, lt
  or or_5 (or_5_out, comparator_6_eq, comparator_19_eq);
  and and_7 (muxy, comparator_19_eq, comparator_8_eq);
  and and_8 (store3, comparator_5_eq, or_5_out);

  // Other names for the same wires on the sheet: B[3:0] = \input 
endmodule
